// Logisim project cpu.circ as structural Verilog: 15 circuits, main circuit COMPUTER
module ALU_1b (
  input  Sub,
  input  Cin,
  input  [2:0] in_3,
  input  A,
  input  B,
  input  Ein,
  input  Lin,
  output Out,
  output Eout,
  output Cout,
  output Lout
);

  wire adder_1_out, and_1_out, and_2_out, nor_1_out, or_1_out, xor_1_out, xor_2_out;

  and and_1 (and_1_out, A, B);
  or or_1 (or_1_out, A, B);
  xor xor_1 (xor_1_out, A, B);
  nor nor_1 (nor_1_out, A, B);
  Adder #(.width(1)) adder_1 (.a(A), .b(xor_2_out), .out(adder_1_out), .cin(Cin), .cout(Cout));
  xor xor_2 (xor_2_out, B, Sub);
  Multiplexer #(.select(3)) multiplexer_1 (
    .in0(adder_1_out), .in1(adder_1_out), .in2(and_1_out), .in3(or_1_out), .in4(xor_1_out), .in5(nor_1_out),
    .out(Out), .sel(in_3));  // open: in6, in7
  and and_2 (and_2_out, xor_1_out, Ein, A);
  and and_3 (Eout, Ein, ~xor_1_out);  // AND_Gate
  or or_2 (Lout, and_2_out, Lin);
endmodule

module ALU_8b (
  input  Sub,
  input  [2:0] Op,
  input  [7:0] A,
  input  [7:0] B,
  output [7:0] Out,
  output [3:0] FLAGS
);

  wire alu_1b_1_cout, alu_1b_2_cout, alu_1b_2_eout, alu_1b_2_lout, alu_1b_3_cout, alu_1b_3_eout,
       alu_1b_3_lout, alu_1b_4_cout, alu_1b_4_eout, alu_1b_4_lout, alu_1b_5_cout, alu_1b_5_eout,
       alu_1b_5_lout, alu_1b_6_cout, alu_1b_6_eout, alu_1b_6_lout, alu_1b_7_cout, alu_1b_7_eout,
       alu_1b_7_lout, alu_1b_8_eout, alu_1b_8_lout;

  ALU_1b alu_1b_1 (
    .A(A[0]), .B(B[0]), .Sub(Sub), .Cin(Sub), .in_3(Op), .Ein(alu_1b_2_eout), .Lin(alu_1b_2_lout),
    .Out(Out[0]), .Eout(FLAGS[1]), .Cout(alu_1b_1_cout), .Lout(FLAGS[2]));
  ALU_1b alu_1b_2 (
    .A(A[1]), .B(B[1]), .Sub(Sub), .Cin(alu_1b_1_cout), .in_3(Op), .Ein(alu_1b_3_eout), .Lin(alu_1b_3_lout),
    .Out(Out[1]), .Eout(alu_1b_2_eout), .Cout(alu_1b_2_cout), .Lout(alu_1b_2_lout));
  ALU_1b alu_1b_3 (
    .A(A[2]), .B(B[2]), .Sub(Sub), .Cin(alu_1b_2_cout), .in_3(Op), .Ein(alu_1b_4_eout), .Lin(alu_1b_4_lout),
    .Out(Out[2]), .Eout(alu_1b_3_eout), .Cout(alu_1b_3_cout), .Lout(alu_1b_3_lout));
  ALU_1b alu_1b_4 (
    .A(A[3]), .B(B[3]), .Sub(Sub), .Cin(alu_1b_3_cout), .in_3(Op), .Ein(alu_1b_5_eout), .Lin(alu_1b_5_lout),
    .Out(Out[3]), .Eout(alu_1b_4_eout), .Cout(alu_1b_4_cout), .Lout(alu_1b_4_lout));
  ALU_1b alu_1b_5 (
    .A(A[4]), .B(B[4]), .Sub(Sub), .Cin(alu_1b_4_cout), .in_3(Op), .Ein(alu_1b_6_eout), .Lin(alu_1b_6_lout),
    .Out(Out[4]), .Eout(alu_1b_5_eout), .Cout(alu_1b_5_cout), .Lout(alu_1b_5_lout));
  ALU_1b alu_1b_6 (
    .A(A[5]), .B(B[5]), .Sub(Sub), .Cin(alu_1b_5_cout), .in_3(Op), .Ein(alu_1b_7_eout), .Lin(alu_1b_7_lout),
    .Out(Out[5]), .Eout(alu_1b_6_eout), .Cout(alu_1b_6_cout), .Lout(alu_1b_6_lout));
  ALU_1b alu_1b_7 (
    .A(A[6]), .B(B[6]), .Sub(Sub), .Cin(alu_1b_6_cout), .in_3(Op), .Ein(alu_1b_8_eout), .Lin(alu_1b_8_lout),
    .Out(Out[6]), .Eout(alu_1b_7_eout), .Cout(alu_1b_7_cout), .Lout(alu_1b_7_lout));
  ALU_1b alu_1b_8 (
    .A(A[7]), .B(B[7]), .Sub(Sub), .Cin(alu_1b_7_cout), .in_3(Op), .Ein(1'b1), .Lin(1'b0), .Out(Out[7]),
    .Eout(alu_1b_8_eout), .Cout(FLAGS[3]), .Lout(alu_1b_8_lout));
  nor nor_1 (FLAGS[0], Out[0], Out[1], Out[2], Out[3], Out[4], Out[5], Out[6], Out[7]);

  // Notes on the sheet:
  //   CLEZ
endmodule

module MEM_1b (
  input  En,
  input  Set,
  output Q,
  output NQ
);

  D_Flip_Flop #(.trigger("high")) d_ff_1 (.D(Set), .clk(En), .Q(Q), .Qn(NQ));  // open: preset, reset
endmodule

module MEM_8b (
  input  [7:0] In,
  input  En,
  output [7:0] Out
);

  MEM_1b mem_1b_1 (.En(En), .Set(In[0]), .Q(Out[0]));  // open: NQ
  MEM_1b mem_1b_2 (.En(En), .Set(In[1]), .Q(Out[1]));  // open: NQ
  MEM_1b mem_1b_3 (.En(En), .Set(In[2]), .Q(Out[2]));  // open: NQ
  MEM_1b mem_1b_4 (.En(En), .Set(In[3]), .Q(Out[3]));  // open: NQ
  MEM_1b mem_1b_5 (.En(En), .Set(In[4]), .Q(Out[4]));  // open: NQ
  MEM_1b mem_1b_6 (.En(En), .Set(In[5]), .Q(Out[5]));  // open: NQ
  MEM_1b mem_1b_7 (.En(En), .Set(In[6]), .Q(Out[6]));  // open: NQ
  MEM_1b mem_1b_8 (.En(En), .Set(In[7]), .Q(Out[7]));  // open: NQ
endmodule

module ENABLER_8b (
  input  [7:0] In,
  input  En,
  output [7:0] Out
);

  and and_1 (Out[0], In[0], En);
  and and_2 (Out[1], In[1], En);
  and and_3 (Out[2], In[2], En);
  and and_4 (Out[3], In[3], En);
  and and_5 (Out[4], In[4], En);
  and and_6 (Out[5], In[5], En);
  and and_7 (Out[6], In[6], En);
  and and_8 (Out[7], In[7], En);
endmodule

module REG_8b (
  input  [7:0] In,
  input  Write,
  input  Read,
  output [7:0] Data,
  output [7:0] Out
);

  wire [7:0] enabler_8b_1_out;

  MEM_8b mem_8b_1 (.In(In), .En(Write), .Out(Data));
  ENABLER_8b enabler_8b_1 (.In(Data), .En(Read), .Out(enabler_8b_1_out));
  assign Out = Read ? enabler_8b_1_out : 8'bz;  // Controlled_Buffer controlled_buffer_1
endmodule

module RAM_CELL_8b (
  input  [7:0] In,
  input  Rst,
  input  H,
  input  V,
  input  Write,
  input  Read,
  output [7:0] Out
);

  wire and_1_out, and_2_out, and_3_out, or_1_out;
  wire [7:0] reg_8b_1_out;

  and and_1 (and_1_out, H, V);
  or or_1 (or_1_out, Rst, and_2_out);
  and and_2 (and_2_out, and_1_out, Write);
  and and_3 (and_3_out, and_1_out, Read);
  assign Out = and_3_out ? reg_8b_1_out : 8'bz;  // Controlled_Buffer controlled_buffer_1
  REG_8b reg_8b_1 (.In(In), .Write(or_1_out), .Read(and_3_out), .Out(reg_8b_1_out));  // open: Data
endmodule

module RAM_64B (
  input  [7:0] In,
  input  [7:0] Addr,
  input  Set_Addr,
  input  Read,
  input  Write,
  input  Reset,
  output [7:0] Out
);

  wire decoder_1_out0, decoder_1_out1, decoder_1_out2, decoder_1_out3, decoder_1_out4, decoder_1_out5,
       decoder_1_out6, decoder_1_out7, decoder_2_out0, decoder_2_out1, decoder_2_out2, decoder_2_out3,
       decoder_2_out4, decoder_2_out5, decoder_2_out6, decoder_2_out7;
  wire [7:0] mem_8b_1_out;

  MEM_8b mem_8b_1 (.In(Addr), .En(Set_Addr), .Out(mem_8b_1_out));
  Decoder #(.enable("false"), .select(3)) decoder_1 (
    .out0(decoder_1_out0), .out1(decoder_1_out1), .out2(decoder_1_out2), .out3(decoder_1_out3),
    .out4(decoder_1_out4), .out5(decoder_1_out5), .out6(decoder_1_out6), .out7(decoder_1_out7),
    .sel(mem_8b_1_out[5:3]));
  RAM_CELL_8b ram_cell_8b_1 (
    .Rst(Reset), .H(decoder_1_out0), .V(decoder_2_out0), .In(In), .Write(Write), .Read(Read), .Out(Out));
  RAM_CELL_8b ram_cell_8b_2 (
    .Rst(Reset), .H(decoder_1_out1), .V(decoder_2_out0), .In(In), .Write(Write), .Read(Read), .Out(Out));
  RAM_CELL_8b ram_cell_8b_3 (
    .Rst(Reset), .H(decoder_1_out2), .V(decoder_2_out0), .In(In), .Write(Write), .Read(Read), .Out(Out));
  RAM_CELL_8b ram_cell_8b_4 (
    .Rst(Reset), .H(decoder_1_out3), .V(decoder_2_out0), .In(In), .Write(Write), .Read(Read), .Out(Out));
  RAM_CELL_8b ram_cell_8b_5 (
    .Rst(Reset), .H(decoder_1_out4), .V(decoder_2_out0), .In(In), .Write(Write), .Read(Read), .Out(Out));
  RAM_CELL_8b ram_cell_8b_6 (
    .Rst(Reset), .H(decoder_1_out5), .V(decoder_2_out0), .In(In), .Write(Write), .Read(Read), .Out(Out));
  RAM_CELL_8b ram_cell_8b_7 (
    .Rst(Reset), .H(decoder_1_out6), .V(decoder_2_out0), .In(In), .Write(Write), .Read(Read), .Out(Out));
  RAM_CELL_8b ram_cell_8b_8 (
    .Rst(Reset), .H(decoder_1_out7), .V(decoder_2_out0), .In(In), .Write(Write), .Read(Read), .Out(Out));
  RAM_CELL_8b ram_cell_8b_9 (
    .Rst(Reset), .H(decoder_1_out0), .V(decoder_2_out1), .In(In), .Write(Write), .Read(Read), .Out(Out));
  RAM_CELL_8b ram_cell_8b_10 (
    .Rst(Reset), .H(decoder_1_out1), .V(decoder_2_out1), .In(In), .Write(Write), .Read(Read), .Out(Out));
  RAM_CELL_8b ram_cell_8b_11 (
    .Rst(Reset), .H(decoder_1_out2), .V(decoder_2_out1), .In(In), .Write(Write), .Read(Read), .Out(Out));
  RAM_CELL_8b ram_cell_8b_12 (
    .Rst(Reset), .H(decoder_1_out3), .V(decoder_2_out1), .In(In), .Write(Write), .Read(Read), .Out(Out));
  RAM_CELL_8b ram_cell_8b_13 (
    .Rst(Reset), .H(decoder_1_out4), .V(decoder_2_out1), .In(In), .Write(Write), .Read(Read), .Out(Out));
  RAM_CELL_8b ram_cell_8b_14 (
    .Rst(Reset), .H(decoder_1_out5), .V(decoder_2_out1), .In(In), .Write(Write), .Read(Read), .Out(Out));
  RAM_CELL_8b ram_cell_8b_15 (
    .Rst(Reset), .H(decoder_1_out6), .V(decoder_2_out1), .In(In), .Write(Write), .Read(Read), .Out(Out));
  RAM_CELL_8b ram_cell_8b_16 (
    .Rst(Reset), .H(decoder_1_out7), .V(decoder_2_out1), .In(In), .Write(Write), .Read(Read), .Out(Out));
  RAM_CELL_8b ram_cell_8b_17 (
    .Rst(Reset), .H(decoder_1_out0), .V(decoder_2_out2), .In(In), .Write(Write), .Read(Read), .Out(Out));
  RAM_CELL_8b ram_cell_8b_18 (
    .Rst(Reset), .H(decoder_1_out1), .V(decoder_2_out2), .In(In), .Write(Write), .Read(Read), .Out(Out));
  RAM_CELL_8b ram_cell_8b_19 (
    .Rst(Reset), .H(decoder_1_out2), .V(decoder_2_out2), .In(In), .Write(Write), .Read(Read), .Out(Out));
  RAM_CELL_8b ram_cell_8b_20 (
    .Rst(Reset), .H(decoder_1_out3), .V(decoder_2_out2), .In(In), .Write(Write), .Read(Read), .Out(Out));
  RAM_CELL_8b ram_cell_8b_21 (
    .Rst(Reset), .H(decoder_1_out4), .V(decoder_2_out2), .In(In), .Write(Write), .Read(Read), .Out(Out));
  RAM_CELL_8b ram_cell_8b_22 (
    .Rst(Reset), .H(decoder_1_out5), .V(decoder_2_out2), .In(In), .Write(Write), .Read(Read), .Out(Out));
  RAM_CELL_8b ram_cell_8b_23 (
    .Rst(Reset), .H(decoder_1_out6), .V(decoder_2_out2), .In(In), .Write(Write), .Read(Read), .Out(Out));
  RAM_CELL_8b ram_cell_8b_24 (
    .Rst(Reset), .H(decoder_1_out7), .V(decoder_2_out2), .In(In), .Write(Write), .Read(Read), .Out(Out));
  Decoder #(.enable("false"), .select(3)) decoder_2 (
    .out0(decoder_2_out0), .out1(decoder_2_out1), .out2(decoder_2_out2), .out3(decoder_2_out3),
    .out4(decoder_2_out4), .out5(decoder_2_out5), .out6(decoder_2_out6), .out7(decoder_2_out7),
    .sel(mem_8b_1_out[2:0]));
  RAM_CELL_8b ram_cell_8b_25 (
    .Rst(Reset), .H(decoder_1_out0), .V(decoder_2_out3), .In(In), .Write(Write), .Read(Read), .Out(Out));
  RAM_CELL_8b ram_cell_8b_26 (
    .Rst(Reset), .H(decoder_1_out1), .V(decoder_2_out3), .In(In), .Write(Write), .Read(Read), .Out(Out));
  RAM_CELL_8b ram_cell_8b_27 (
    .Rst(Reset), .H(decoder_1_out2), .V(decoder_2_out3), .In(In), .Write(Write), .Read(Read), .Out(Out));
  RAM_CELL_8b ram_cell_8b_28 (
    .Rst(Reset), .H(decoder_1_out3), .V(decoder_2_out3), .In(In), .Write(Write), .Read(Read), .Out(Out));
  RAM_CELL_8b ram_cell_8b_29 (
    .Rst(Reset), .H(decoder_1_out4), .V(decoder_2_out3), .In(In), .Write(Write), .Read(Read), .Out(Out));
  RAM_CELL_8b ram_cell_8b_30 (
    .Rst(Reset), .H(decoder_1_out5), .V(decoder_2_out3), .In(In), .Write(Write), .Read(Read), .Out(Out));
  RAM_CELL_8b ram_cell_8b_31 (
    .Rst(Reset), .H(decoder_1_out6), .V(decoder_2_out3), .In(In), .Write(Write), .Read(Read), .Out(Out));
  RAM_CELL_8b ram_cell_8b_32 (
    .Rst(Reset), .H(decoder_1_out7), .V(decoder_2_out3), .In(In), .Write(Write), .Read(Read), .Out(Out));
  RAM_CELL_8b ram_cell_8b_33 (
    .Rst(Reset), .H(decoder_1_out0), .V(decoder_2_out4), .In(In), .Write(Write), .Read(Read), .Out(Out));
  RAM_CELL_8b ram_cell_8b_34 (
    .Rst(Reset), .H(decoder_1_out1), .V(decoder_2_out4), .In(In), .Write(Write), .Read(Read), .Out(Out));
  RAM_CELL_8b ram_cell_8b_35 (
    .Rst(Reset), .H(decoder_1_out2), .V(decoder_2_out4), .In(In), .Write(Write), .Read(Read), .Out(Out));
  RAM_CELL_8b ram_cell_8b_36 (
    .Rst(Reset), .H(decoder_1_out3), .V(decoder_2_out4), .In(In), .Write(Write), .Read(Read), .Out(Out));
  RAM_CELL_8b ram_cell_8b_37 (
    .Rst(Reset), .H(decoder_1_out4), .V(decoder_2_out4), .In(In), .Write(Write), .Read(Read), .Out(Out));
  RAM_CELL_8b ram_cell_8b_38 (
    .Rst(Reset), .H(decoder_1_out5), .V(decoder_2_out4), .In(In), .Write(Write), .Read(Read), .Out(Out));
  RAM_CELL_8b ram_cell_8b_39 (
    .Rst(Reset), .H(decoder_1_out6), .V(decoder_2_out4), .In(In), .Write(Write), .Read(Read), .Out(Out));
  RAM_CELL_8b ram_cell_8b_40 (
    .Rst(Reset), .H(decoder_1_out7), .V(decoder_2_out4), .In(In), .Write(Write), .Read(Read), .Out(Out));
  RAM_CELL_8b ram_cell_8b_41 (
    .Rst(Reset), .H(decoder_1_out0), .V(decoder_2_out5), .In(In), .Write(Write), .Read(Read), .Out(Out));
  RAM_CELL_8b ram_cell_8b_42 (
    .Rst(Reset), .H(decoder_1_out1), .V(decoder_2_out5), .In(In), .Write(Write), .Read(Read), .Out(Out));
  RAM_CELL_8b ram_cell_8b_43 (
    .Rst(Reset), .H(decoder_1_out2), .V(decoder_2_out5), .In(In), .Write(Write), .Read(Read), .Out(Out));
  RAM_CELL_8b ram_cell_8b_44 (
    .Rst(Reset), .H(decoder_1_out3), .V(decoder_2_out5), .In(In), .Write(Write), .Read(Read), .Out(Out));
  RAM_CELL_8b ram_cell_8b_45 (
    .Rst(Reset), .H(decoder_1_out4), .V(decoder_2_out5), .In(In), .Write(Write), .Read(Read), .Out(Out));
  RAM_CELL_8b ram_cell_8b_46 (
    .Rst(Reset), .H(decoder_1_out5), .V(decoder_2_out5), .In(In), .Write(Write), .Read(Read), .Out(Out));
  RAM_CELL_8b ram_cell_8b_47 (
    .Rst(Reset), .H(decoder_1_out6), .V(decoder_2_out5), .In(In), .Write(Write), .Read(Read), .Out(Out));
  RAM_CELL_8b ram_cell_8b_48 (
    .Rst(Reset), .H(decoder_1_out7), .V(decoder_2_out5), .In(In), .Write(Write), .Read(Read), .Out(Out));
  RAM_CELL_8b ram_cell_8b_49 (
    .Rst(Reset), .H(decoder_1_out0), .V(decoder_2_out6), .In(In), .Write(Write), .Read(Read), .Out(Out));
  RAM_CELL_8b ram_cell_8b_50 (
    .Rst(Reset), .H(decoder_1_out1), .V(decoder_2_out6), .In(In), .Write(Write), .Read(Read), .Out(Out));
  RAM_CELL_8b ram_cell_8b_51 (
    .Rst(Reset), .H(decoder_1_out2), .V(decoder_2_out6), .In(In), .Write(Write), .Read(Read), .Out(Out));
  RAM_CELL_8b ram_cell_8b_52 (
    .Rst(Reset), .H(decoder_1_out3), .V(decoder_2_out6), .In(In), .Write(Write), .Read(Read), .Out(Out));
  RAM_CELL_8b ram_cell_8b_53 (
    .Rst(Reset), .H(decoder_1_out4), .V(decoder_2_out6), .In(In), .Write(Write), .Read(Read), .Out(Out));
  RAM_CELL_8b ram_cell_8b_54 (
    .Rst(Reset), .H(decoder_1_out5), .V(decoder_2_out6), .In(In), .Write(Write), .Read(Read), .Out(Out));
  RAM_CELL_8b ram_cell_8b_55 (
    .Rst(Reset), .H(decoder_1_out6), .V(decoder_2_out6), .In(In), .Write(Write), .Read(Read), .Out(Out));
  RAM_CELL_8b ram_cell_8b_56 (
    .Rst(Reset), .H(decoder_1_out7), .V(decoder_2_out6), .In(In), .Write(Write), .Read(Read), .Out(Out));
  RAM_CELL_8b ram_cell_8b_57 (
    .Rst(Reset), .H(decoder_1_out0), .V(decoder_2_out7), .In(In), .Write(Write), .Read(Read), .Out(Out));
  RAM_CELL_8b ram_cell_8b_58 (
    .Rst(Reset), .H(decoder_1_out1), .V(decoder_2_out7), .In(In), .Write(Write), .Read(Read), .Out(Out));
  RAM_CELL_8b ram_cell_8b_59 (
    .Rst(Reset), .H(decoder_1_out2), .V(decoder_2_out7), .In(In), .Write(Write), .Read(Read), .Out(Out));
  RAM_CELL_8b ram_cell_8b_60 (
    .Rst(Reset), .H(decoder_1_out3), .V(decoder_2_out7), .In(In), .Write(Write), .Read(Read), .Out(Out));
  RAM_CELL_8b ram_cell_8b_61 (
    .Rst(Reset), .H(decoder_1_out4), .V(decoder_2_out7), .In(In), .Write(Write), .Read(Read), .Out(Out));
  RAM_CELL_8b ram_cell_8b_62 (
    .Rst(Reset), .H(decoder_1_out5), .V(decoder_2_out7), .In(In), .Write(Write), .Read(Read), .Out(Out));
  RAM_CELL_8b ram_cell_8b_63 (
    .Rst(Reset), .H(decoder_1_out6), .V(decoder_2_out7), .In(In), .Write(Write), .Read(Read), .Out(Out));
  RAM_CELL_8b ram_cell_8b_64 (
    .Rst(Reset), .H(decoder_1_out7), .V(decoder_2_out7), .In(In), .Write(Write), .Read(Read), .Out(Out));

  // Notes on the sheet:
  //   MEM REG
endmodule

module CLK_TIMER (
  input  CLK_In_15818b0f,
  output out_2,
  output CLKW,
  output CLKR
);

  wire j_k_ff_1_qn;

  J_K_Flip_Flop j_k_ff_1 (
    .J(1'b1), .K(1'b1), .clk(CLK_In_15818b0f), .Q(out_2), .Qn(j_k_ff_1_qn));  // open: preset, reset
  and and_1 (CLKW, CLK_In_15818b0f, out_2);
  nand nand_1 (CLKR, j_k_ff_1_qn, CLK_In_15818b0f);
endmodule

module STEP (
  input  CLK,
  output S0,
  output S1,
  output S2,
  output S3,
  output S4,
  output S5
);

  wire mem_1b_1_q, mem_1b_2_q, mem_1b_3_q, mem_1b_4_q, mem_1b_5_q, mem_1b_6_q, mem_1b_7_q, mem_1b_8_q,
       mem_1b_9_q, mem_1b_10_q, mem_1b_11_q, mem_1b_12_q, not_1_out, not_2_out, not_3_out, not_4_out,
       not_5_out, not_6_out, not_7_out, or_2_out, or_3_out;

  not not_1 (not_1_out, mem_1b_12_q);
  not not_2 (not_2_out, CLK);
  or or_1 (S0, mem_1b_12_q, not_3_out);
  or or_2 (or_2_out, mem_1b_12_q, CLK);
  or or_3 (or_3_out, mem_1b_12_q, not_2_out);
  not not_3 (not_3_out, mem_1b_2_q);
  MEM_1b mem_1b_1 (.En(or_2_out), .Set(not_1_out), .Q(mem_1b_1_q));  // open: NQ
  MEM_1b mem_1b_2 (.En(or_3_out), .Set(mem_1b_1_q), .Q(mem_1b_2_q));  // open: NQ
  and and_1 (S1, mem_1b_2_q, not_4_out);
  not not_4 (not_4_out, mem_1b_4_q);
  MEM_1b mem_1b_3 (.En(or_2_out), .Set(mem_1b_2_q), .Q(mem_1b_3_q));  // open: NQ
  MEM_1b mem_1b_4 (.En(or_3_out), .Set(mem_1b_3_q), .Q(mem_1b_4_q));  // open: NQ
  and and_2 (S2, mem_1b_4_q, not_5_out);
  not not_5 (not_5_out, mem_1b_6_q);
  MEM_1b mem_1b_5 (.En(or_2_out), .Set(mem_1b_4_q), .Q(mem_1b_5_q));  // open: NQ
  MEM_1b mem_1b_6 (.En(or_3_out), .Set(mem_1b_5_q), .Q(mem_1b_6_q));  // open: NQ
  and and_3 (S3, mem_1b_6_q, not_6_out);
  not not_6 (not_6_out, mem_1b_8_q);
  MEM_1b mem_1b_7 (.En(or_2_out), .Set(mem_1b_6_q), .Q(mem_1b_7_q));  // open: NQ
  MEM_1b mem_1b_8 (.En(or_3_out), .Set(mem_1b_7_q), .Q(mem_1b_8_q));  // open: NQ
  and and_4 (S4, mem_1b_8_q, not_7_out);
  not not_7 (not_7_out, mem_1b_10_q);
  MEM_1b mem_1b_9 (.En(or_2_out), .Set(mem_1b_8_q), .Q(mem_1b_9_q));  // open: NQ
  MEM_1b mem_1b_10 (.En(or_3_out), .Set(mem_1b_9_q), .Q(mem_1b_10_q));  // open: NQ
  or or_4 (S5, mem_1b_10_q, mem_1b_12_q);
  MEM_1b mem_1b_11 (.En(or_2_out), .Set(mem_1b_10_q), .Q(mem_1b_11_q));  // open: NQ
  MEM_1b mem_1b_12 (.En(or_3_out), .Set(mem_1b_11_q), .Q(mem_1b_12_q));  // open: NQ
endmodule

module FLAGS_REG (
  input  [3:0] F_IN,
  input  RST,
  input  W,
  output [3:0] F_OUT
);

  wire or_1_out;
  wire [7:0] multiplexer_1_out;
  wire [7:4] reg_8b_1_out;

  Multiplexer #(.width(8)) multiplexer_1 (.in0({4'b0000, F_IN}), .in1({8{1'b0}}), .out(multiplexer_1_out), .sel(RST));
  or or_1 (or_1_out, RST, W);
  REG_8b reg_8b_1 (.In(multiplexer_1_out), .Write(or_1_out), .Read(1'b1), .Out({reg_8b_1_out, F_OUT}));  // open: Data
endmodule

module BUS_SET_INC (
  input  Enable,
  input  [7:0] In,
  output [7:0] Out
);

  wire not_1_out;

  not not_1 (not_1_out, Enable);
  or or_1 (Out[0], Enable, In[0]);
  and and_1 (Out[1], not_1_out, In[1]);
  and and_2 (Out[2], not_1_out, In[2]);
  and and_3 (Out[3], not_1_out, In[3]);
  and and_4 (Out[4], not_1_out, In[4]);
  and and_5 (Out[5], not_1_out, In[5]);
  and and_6 (Out[6], not_1_out, In[6]);
  and and_7 (Out[7], not_1_out, In[7]);
endmodule

module CU (
  input  CLK,
  input  CLKR,
  input  CLKW,
  input  [3:0] FLAGS,
  input  [7:0] INSTRUCTION_CODE_IN,
  output MAR_W,
  output ADDR_INC,
  output RAM_R,
  output ACC_W,
  output ACC_R,
  output IAR_W,
  output IAR_R,
  output IR_W,
  output TMP_W,
  output RAM_W,
  output HLT,
  output R0_W,
  output R1_W,
  output R2_W,
  output R3_W,
  output R0_R,
  output SET_FLAGS,
  output R1_R,
  output RST_FLAGS,
  output R2_R,
  output R3_R,
  output [2:0] ALU_OP
);

  wire ACC_R_t, ACC_W_t, ALU_SET_OP, and_4_out, and_5_out, and_6_out, and_7_out, and_8_out, and_9_out,
       and_10_out, and_11_out, and_29_out, and_30_out, and_31_out, and_32_out, and_33_out, and_34_out,
       and_35_out, and_36_out, and_37_out, and_38_out, and_39_out, and_40_out, and_41_out, and_42_out,
       and_43_out, and_44_out, and_45_out, and_46_out, and_47_out, and_48_out, C_out, CLF, decoder_1_out0,
       decoder_1_out1, decoder_1_out2, decoder_1_out3, decoder_2_out0, decoder_2_out1, decoder_2_out2,
       decoder_2_out3, decoder_3_out0, decoder_3_out1, decoder_3_out2, decoder_3_out3, E_out, FLAGS_RST,
       FLAGS_W, IAR_R_t, IAR_W_t, IR_W_t, IS_IR_INC, JMP, JMP_CONDITIONAL, JMP_IF, JMPR, L_out, LDD, LDR,
       MAR_W_t, MOV, RAM_R_t, RAM_W_t, REG_A_R, REG_A_W, REG_B_R, SDR, step_1_s0, step_1_s2, T3, T4, T5,
       TMP_W_t, Z_out;

  or or_1 (R0_R, and_4_out, and_8_out);
  or or_2 (R1_R, and_5_out, and_9_out);
  or or_3 (R2_R, and_6_out, and_10_out);
  or or_4 (R3_R, and_7_out, and_11_out);
  Pull_Resistor pull_resistor_1 (.node(ADDR_INC));
  and and_1 (RAM_R, CLKR, RAM_R_t);
  and and_2 (ACC_R, CLKR, ACC_R_t);
  and and_3 (IAR_R, CLKR, IAR_R_t);
  and and_4 (and_4_out, CLKR, REG_B_R, decoder_1_out0);
  and and_5 (and_5_out, CLKR, REG_B_R, decoder_1_out1);
  and and_6 (and_6_out, CLKR, REG_B_R, decoder_1_out2);
  and and_7 (and_7_out, CLKR, REG_B_R, decoder_1_out3);
  and and_8 (and_8_out, CLKR, REG_A_R, decoder_2_out0);
  and and_9 (and_9_out, CLKR, REG_A_R, decoder_2_out1);
  and and_10 (and_10_out, CLKR, REG_A_R, decoder_2_out2);
  and and_11 (and_11_out, CLKR, REG_A_R, decoder_2_out3);
  Pull_Resistor pull_resistor_2 (.node(RAM_R_t));
  Pull_Resistor pull_resistor_3 (.node(ACC_R_t));
  Pull_Resistor pull_resistor_4 (.node(IAR_R_t));
  Pull_Resistor pull_resistor_5 (.node(REG_B_R));
  Pull_Resistor pull_resistor_6 (.node(REG_A_R));
  Decoder #(.enable("false"), .select(2)) decoder_1 (
    .out0(decoder_1_out0), .out1(decoder_1_out1), .out2(decoder_1_out2), .out3(decoder_1_out3),
    .sel(INSTRUCTION_CODE_IN[1:0]));
  Decoder #(.enable("false"), .select(2)) decoder_2 (
    .out0(decoder_2_out0), .out1(decoder_2_out1), .out2(decoder_2_out2), .out3(decoder_2_out3),
    .sel(INSTRUCTION_CODE_IN[3:2]));
  and and_12 (ALU_OP[0], ALU_SET_OP, INSTRUCTION_CODE_IN[4], INSTRUCTION_CODE_IN[7]);
  and and_13 (ALU_OP[1], ALU_SET_OP, INSTRUCTION_CODE_IN[5], INSTRUCTION_CODE_IN[7]);
  and and_14 (ALU_OP[2], ALU_SET_OP, INSTRUCTION_CODE_IN[6], INSTRUCTION_CODE_IN[7]);
  STEP step_1 (.CLK(CLK), .S4(T4), .S5(T5), .S0(step_1_s0), .S1(IR_W_t), .S2(step_1_s2), .S3(T3));
  Pull_Resistor pull_resistor_7 (.node(ALU_SET_OP));
  and and_15 (IS_IR_INC, ~T3, ~T4, ~T5);  // AND_Gate
  assign ADDR_INC = IS_IR_INC ? step_1_s0 : 1'bz;  // Controlled_Buffer controlled_buffer_1
  assign IAR_R_t = IS_IR_INC ? step_1_s0 : 1'bz;  // Controlled_Buffer controlled_buffer_2
  assign MAR_W_t = IS_IR_INC ? step_1_s0 : 1'bz;  // Controlled_Buffer controlled_buffer_3
  assign ACC_W_t = IS_IR_INC ? step_1_s0 : 1'bz;  // Controlled_Buffer controlled_buffer_4
  and C (C_out, FLAGS[3], INSTRUCTION_CODE_IN[3]);
  and L (L_out, FLAGS[2], INSTRUCTION_CODE_IN[2]);
  and E (E_out, FLAGS[1], INSTRUCTION_CODE_IN[1]);
  and Z (Z_out, FLAGS[0], INSTRUCTION_CODE_IN[0]);
  assign RAM_R_t = IS_IR_INC ? IR_W_t : 1'bz;  // Controlled_Buffer controlled_buffer_5
  and and_16 (HLT, INSTRUCTION_CODE_IN[7], ~INSTRUCTION_CODE_IN[4], INSTRUCTION_CODE_IN[5], INSTRUCTION_CODE_IN[6]);  // AND_Gate
  or or_5 (JMP_CONDITIONAL, C_out, L_out, E_out, Z_out);
  assign ACC_R_t = IS_IR_INC ? step_1_s2 : 1'bz;  // Controlled_Buffer controlled_buffer_6
  assign IAR_W_t = IS_IR_INC ? step_1_s2 : 1'bz;  // Controlled_Buffer controlled_buffer_7
  Pull_Resistor pull_resistor_8 (.node(MAR_W_t));
  Pull_Resistor pull_resistor_9 (.node(ACC_W_t));
  Pull_Resistor pull_resistor_10 (.node(IAR_W_t));
  Pull_Resistor pull_resistor_11 (.node(IR_W_t));
  Pull_Resistor pull_resistor_12 (.node(TMP_W_t));
  Pull_Resistor pull_resistor_13 (.node(RAM_W_t));
  Pull_Resistor pull_resistor_14 (.node(REG_A_W));
  Decoder #(.enable("false"), .select(2)) decoder_3 (
    .out0(decoder_3_out0), .out1(decoder_3_out1), .out2(decoder_3_out2), .out3(decoder_3_out3),
    .sel(INSTRUCTION_CODE_IN[3:2]));
  Pull_Resistor pull_resistor_15 (.node(FLAGS_W));
  Pull_Resistor pull_resistor_16 (.node(FLAGS_RST));
  and and_17 (MAR_W, CLKW, MAR_W_t);
  and and_18 (ACC_W, CLKW, ACC_W_t);
  and and_19 (IAR_W, CLKW, IAR_W_t);
  and and_20 (IR_W, CLKW, IR_W_t);
  and and_21 (TMP_W, CLKW, TMP_W_t);
  and and_22 (RAM_W, CLKW, RAM_W_t);
  and and_23 (R0_W, CLKW, REG_A_W, decoder_3_out0);
  and and_24 (R1_W, CLKW, REG_A_W, decoder_3_out1);
  and and_25 (R2_W, CLKW, REG_A_W, decoder_3_out2);
  and and_26 (R3_W, CLKW, REG_A_W, decoder_3_out3);
  and and_27 (SET_FLAGS, CLKW, FLAGS_W);
  and and_28 (RST_FLAGS, CLKW, FLAGS_RST);
  and and_29 (and_29_out, ~IS_IR_INC, INSTRUCTION_CODE_IN[7]);  // AND_Gate
  and and_30 (and_30_out, ~IS_IR_INC, ~INSTRUCTION_CODE_IN[7]);  // AND_Gate
  Decoder #(.select(3)) decoder_4 (
    .out0(LDR), .out1(SDR), .out2(LDD), .out3(MOV), .out4(JMPR), .out5(JMP), .out6(JMP_IF), .out7(CLF),
    .sel(INSTRUCTION_CODE_IN[6:4]), .en(and_30_out));
  and and_31 (and_31_out, T3, and_29_out);
  and and_32 (and_32_out, T4, and_29_out);
  and and_33 (and_33_out, and_29_out, T5);
  assign REG_B_R = and_29_out ? and_31_out : 1'bz;  // Controlled_Buffer controlled_buffer_8
  assign TMP_W_t = and_29_out ? and_31_out : 1'bz;  // Controlled_Buffer controlled_buffer_9
  assign ALU_SET_OP = and_29_out ? and_32_out : 1'bz;  // Controlled_Buffer controlled_buffer_10
  assign REG_A_R = and_29_out ? and_32_out : 1'bz;  // Controlled_Buffer controlled_buffer_11
  assign ACC_W_t = and_29_out ? and_32_out : 1'bz;  // Controlled_Buffer controlled_buffer_12
  assign FLAGS_W = and_29_out ? and_32_out : 1'bz;  // Controlled_Buffer controlled_buffer_13
  assign ACC_R_t = and_29_out ? and_33_out : 1'bz;  // Controlled_Buffer controlled_buffer_14
  assign REG_A_W = and_29_out ? and_33_out : 1'bz;  // Controlled_Buffer controlled_buffer_15
  and and_34 (and_34_out, LDR, T3);
  and and_35 (and_35_out, LDR, T4);
  and and_36 (and_36_out, SDR, T3);
  and and_37 (and_37_out, SDR, T4);
  and and_38 (and_38_out, LDD, T3);
  and and_39 (and_39_out, LDD, T4);
  and and_40 (and_40_out, LDD, T5);
  and and_41 (and_41_out, MOV, T3);
  assign REG_B_R = LDR ? and_34_out : 1'bz;  // Controlled_Buffer controlled_buffer_16
  assign MAR_W_t = LDR ? and_34_out : 1'bz;  // Controlled_Buffer controlled_buffer_17
  assign RAM_R_t = LDR ? and_35_out : 1'bz;  // Controlled_Buffer controlled_buffer_18
  assign REG_A_W = LDR ? and_35_out : 1'bz;  // Controlled_Buffer controlled_buffer_19
  assign REG_B_R = SDR ? and_36_out : 1'bz;  // Controlled_Buffer controlled_buffer_20
  assign MAR_W_t = SDR ? and_36_out : 1'bz;  // Controlled_Buffer controlled_buffer_21
  assign REG_A_R = SDR ? and_37_out : 1'bz;  // Controlled_Buffer controlled_buffer_22
  assign RAM_W_t = SDR ? and_37_out : 1'bz;  // Controlled_Buffer controlled_buffer_23
  assign IAR_R_t = LDD ? and_38_out : 1'bz;  // Controlled_Buffer controlled_buffer_24
  assign MAR_W_t = LDD ? and_38_out : 1'bz;  // Controlled_Buffer controlled_buffer_25
  assign ADDR_INC = LDD ? and_38_out : 1'bz;  // Controlled_Buffer controlled_buffer_26
  assign ACC_W_t = LDD ? and_38_out : 1'bz;  // Controlled_Buffer controlled_buffer_27
  assign RAM_R_t = LDD ? and_39_out : 1'bz;  // Controlled_Buffer controlled_buffer_28
  assign REG_A_W = LDD ? and_39_out : 1'bz;  // Controlled_Buffer controlled_buffer_29
  assign ACC_R_t = LDD ? and_40_out : 1'bz;  // Controlled_Buffer controlled_buffer_30
  assign IAR_W_t = LDD ? and_40_out : 1'bz;  // Controlled_Buffer controlled_buffer_31
  assign REG_B_R = MOV ? and_41_out : 1'bz;  // Controlled_Buffer controlled_buffer_32
  assign REG_A_W = MOV ? and_41_out : 1'bz;  // Controlled_Buffer controlled_buffer_33
  and and_42 (and_42_out, JMPR, T3);
  and and_43 (and_43_out, JMP, T3);
  and and_44 (and_44_out, JMP, T4);
  and and_45 (and_45_out, JMP_IF, T3);
  and and_46 (and_46_out, JMP_IF, T4);
  and and_47 (and_47_out, JMP_IF, T5, JMP_CONDITIONAL);
  and and_48 (and_48_out, CLF, T3);
  assign REG_A_R = JMPR ? and_42_out : 1'bz;  // Controlled_Buffer controlled_buffer_34
  assign IAR_W_t = JMPR ? and_42_out : 1'bz;  // Controlled_Buffer controlled_buffer_35
  assign IAR_R_t = JMP ? and_43_out : 1'bz;  // Controlled_Buffer controlled_buffer_36
  assign MAR_W_t = JMP ? and_43_out : 1'bz;  // Controlled_Buffer controlled_buffer_37
  assign RAM_R_t = JMP ? and_44_out : 1'bz;  // Controlled_Buffer controlled_buffer_38
  assign IAR_W_t = JMP ? and_44_out : 1'bz;  // Controlled_Buffer controlled_buffer_39
  assign IAR_R_t = JMP_IF ? and_45_out : 1'bz;  // Controlled_Buffer controlled_buffer_40
  assign MAR_W_t = JMP_IF ? and_45_out : 1'bz;  // Controlled_Buffer controlled_buffer_41
  assign ADDR_INC = JMP_IF ? and_45_out : 1'bz;  // Controlled_Buffer controlled_buffer_42
  assign ACC_W_t = JMP_IF ? and_45_out : 1'bz;  // Controlled_Buffer controlled_buffer_43
  assign ACC_R_t = JMP_IF ? and_46_out : 1'bz;  // Controlled_Buffer controlled_buffer_44
  assign IAR_W_t = and_46_out ? and_46_out : 1'bz;  // Controlled_Buffer controlled_buffer_45
  assign RAM_R_t = JMP_IF ? and_47_out : 1'bz;  // Controlled_Buffer controlled_buffer_46
  assign IAR_W_t = and_47_out ? and_47_out : 1'bz;  // Controlled_Buffer controlled_buffer_47
  assign FLAGS_RST = CLF ? and_48_out : 1'bz;  // Controlled_Buffer controlled_buffer_48

  // Other names for the same wires on the sheet: INSTR_CODE[2:0] = INSTRUCTION_CODE_IN[6:4];
  //   IS_ALU_INSTR = INSTRUCTION_CODE_IN[7]

  // Notes on the sheet:
  //   REG_B
  //   REG_A
  //   CLEZ
  //   REG_A
endmodule

module CPU (
  input  Reset,
  input  LOAD_PROGRAM,
  input  [7:0] PROGRAM_IN,
  input  CLK,
  input  [7:0] PROGRAM_ADDR,
  output [7:0] TMP,
  output [7:0] BUS_DATA,
  output [7:0] R0,
  output [7:0] R1,
  output [7:0] R2,
  output [7:0] R3,
  output HLT,
  output [7:0] ACC,
  output [3:0] FLAGS,
  output [7:0] IAR,
  output [7:0] IR
);

  wire and_1_out, and_2_out, and_3_out, clk_timer_1_clkr, clk_timer_1_clkw, clk_timer_1_out_2, cu_1_acc_r,
       cu_1_acc_w, cu_1_addr_inc, cu_1_iar_r, cu_1_iar_w, cu_1_ir_w, cu_1_mar_w, cu_1_r0_r, cu_1_r0_w,
       cu_1_r1_r, cu_1_r1_w, cu_1_r2_r, cu_1_r2_w, cu_1_r3_r, cu_1_r3_w, cu_1_ram_r, cu_1_ram_w,
       cu_1_rst_flags, cu_1_set_flags, cu_1_tmp_w, not_1_out, not_2_out, or_1_out, or_2_out;
  wire [2:0] cu_1_alu_op;
  wire [3:0] alu_8b_1_flags;
  wire [7:0] alu_8b_1_out, bus_set_inc_1_out, multiplexer_1_out, multiplexer_2_out, reg_8b_6_out;

  ALU_8b alu_8b_1 (
    .B(bus_set_inc_1_out), .A(BUS_DATA), .Sub(and_1_out), .Op(cu_1_alu_op), .Out(alu_8b_1_out),
    .FLAGS(alu_8b_1_flags));
  REG_8b reg_8b_1 (.In(BUS_DATA), .Write(cu_1_tmp_w), .Read(1'b1), .Out(TMP));  // open: Data
  BUS_SET_INC bus_set_inc_1 (.In(TMP), .Enable(cu_1_addr_inc), .Out(bus_set_inc_1_out));
  and and_1 (and_1_out, cu_1_alu_op[0], not_1_out, not_2_out);
  REG_8b reg_8b_2 (.In(alu_8b_1_out), .Write(cu_1_acc_w), .Read(cu_1_acc_r), .Data(ACC), .Out(BUS_DATA));
  not not_1 (not_1_out, cu_1_alu_op[1]);
  not not_2 (not_2_out, cu_1_alu_op[2]);
  FLAGS_REG flags_reg_1 (.F_IN(alu_8b_1_flags), .RST(cu_1_rst_flags), .W(cu_1_set_flags), .F_OUT(FLAGS));
  and and_2 (and_2_out, CLK, ~HLT, ~LOAD_PROGRAM);  // AND_Gate
  CLK_TIMER clk_timer_1 (
    .CLK_In_15818b0f(and_2_out), .out_2(clk_timer_1_out_2), .CLKW(clk_timer_1_clkw), .CLKR(clk_timer_1_clkr));
  REG_8b reg_8b_3 (.In(BUS_DATA), .Write(cu_1_r0_w), .Read(cu_1_r0_r), .Data(R0), .Out(BUS_DATA));
  REG_8b reg_8b_4 (.In(BUS_DATA), .Write(cu_1_iar_w), .Read(cu_1_iar_r), .Data(IAR), .Out(BUS_DATA));
  REG_8b reg_8b_5 (.In(BUS_DATA), .Write(cu_1_r1_w), .Read(cu_1_r1_r), .Data(R1), .Out(BUS_DATA));
  REG_8b reg_8b_6 (.In(BUS_DATA), .Write(cu_1_ir_w), .Read(1'b1), .Data(IR), .Out(reg_8b_6_out));
  CU cu_1 (
    .CLK(clk_timer_1_out_2), .CLKR(clk_timer_1_clkr), .CLKW(clk_timer_1_clkw),
    .INSTRUCTION_CODE_IN(reg_8b_6_out), .FLAGS(FLAGS), .MAR_W(cu_1_mar_w), .ACC_W(cu_1_acc_w),
    .IAR_W(cu_1_iar_w), .IR_W(cu_1_ir_w), .TMP_W(cu_1_tmp_w), .RAM_W(cu_1_ram_w), .R0_W(cu_1_r0_w),
    .R1_W(cu_1_r1_w), .R2_W(cu_1_r2_w), .R3_W(cu_1_r3_w), .SET_FLAGS(cu_1_set_flags),
    .RST_FLAGS(cu_1_rst_flags), .R0_R(cu_1_r0_r), .R1_R(cu_1_r1_r), .R2_R(cu_1_r2_r), .R3_R(cu_1_r3_r),
    .ADDR_INC(cu_1_addr_inc), .RAM_R(cu_1_ram_r), .ACC_R(cu_1_acc_r), .IAR_R(cu_1_iar_r),
    .ALU_OP(cu_1_alu_op), .HLT(HLT));
  REG_8b reg_8b_7 (.In(BUS_DATA), .Write(cu_1_r2_w), .Read(cu_1_r2_r), .Data(R2), .Out(BUS_DATA));
  or or_1 (or_1_out, LOAD_PROGRAM, cu_1_mar_w);
  REG_8b reg_8b_8 (.In(BUS_DATA), .Write(cu_1_r3_w), .Read(cu_1_r3_r), .Data(R3), .Out(BUS_DATA));
  or or_2 (or_2_out, cu_1_ram_w, and_3_out);
  and and_3 (and_3_out, CLK, LOAD_PROGRAM);
  Multiplexer #(.width(8)) multiplexer_1 (
    .in0(BUS_DATA), .in1(PROGRAM_ADDR), .out(multiplexer_1_out), .sel(LOAD_PROGRAM));
  Multiplexer #(.width(8)) multiplexer_2 (
    .in0(BUS_DATA), .in1(PROGRAM_IN), .out(multiplexer_2_out), .sel(LOAD_PROGRAM));
  RAM_64B ram_64b_1 (
    .Addr(multiplexer_1_out), .Set_Addr(or_1_out), .In(multiplexer_2_out), .Read(cu_1_ram_r),
    .Write(or_2_out), .Reset(Reset), .Out(BUS_DATA));

  // Notes on the sheet:
  //   TMP
  //   ACC
  //   R0
  //   IAR
  //   R1
  //   IR
  //   R2
  //   R3
endmodule

module COMPUTER (
  input  in_1
);

  wire button_1_out, clock_1_out, cpu_1_hlt;
  wire [3:0] cpu_1_acc, cpu_1_acc_2, cpu_1_bus_data, cpu_1_bus_data_2, cpu_1_flags, cpu_1_ir, cpu_1_ir_2;
  wire [7:0] counter_1_q, cpu_1_iar, cpu_1_r0, cpu_1_r1, cpu_1_r2, cpu_1_r3, cpu_1_tmp, rom_1_data;

  Counter #(.max('h3f), .ongoal("stay"), .trigger("falling")) counter_1 (
    .clr(button_1_out), .up(in_1), .count(in_1), .clk(clock_1_out), .Q(counter_1_q));  // open: load, D, carry
  ROM rom_1 (.addr(counter_1_q), .data(rom_1_data));
  ROM rom_2 ();  // open: addr, data
  Clock clock_1 (.out(clock_1_out));
  Button button_1 (.out(button_1_out));
  LED led_1 (.in(cpu_1_hlt));
  CPU cpu_1 (
    .Reset(button_1_out), .LOAD_PROGRAM(in_1), .PROGRAM_IN(rom_1_data), .CLK(clock_1_out),
    .PROGRAM_ADDR(counter_1_q), .TMP(cpu_1_tmp), .BUS_DATA({cpu_1_bus_data_2, cpu_1_bus_data}),
    .R0(cpu_1_r0), .R1(cpu_1_r1), .R2(cpu_1_r2), .R3(cpu_1_r3), .HLT(cpu_1_hlt),
    .ACC({cpu_1_acc_2, cpu_1_acc}), .FLAGS(cpu_1_flags), .IAR(cpu_1_iar), .IR({cpu_1_ir_2, cpu_1_ir}));
  Hex_Digit_Display hex_digit_display_1 (.value(cpu_1_tmp[7:4]));  // open: dp
  Hex_Digit_Display hex_digit_display_2 (.value(cpu_1_iar[7:4]));  // open: dp
  Hex_Digit_Display hex_digit_display_3 (.value(cpu_1_r0[7:4]));  // open: dp
  Hex_Digit_Display hex_digit_display_4 (.value(cpu_1_r1[7:4]));  // open: dp
  Hex_Digit_Display hex_digit_display_5 (.value(cpu_1_r2[7:4]));  // open: dp
  Hex_Digit_Display hex_digit_display_6 (.value(cpu_1_r3[7:4]));  // open: dp
  Hex_Digit_Display hex_digit_display_7 (.value(cpu_1_tmp[3:0]));  // open: dp
  Hex_Digit_Display hex_digit_display_8 (.value(cpu_1_iar[3:0]));  // open: dp
  Hex_Digit_Display hex_digit_display_9 (.value(cpu_1_r0[3:0]));  // open: dp
  Hex_Digit_Display hex_digit_display_10 (.value(cpu_1_r1[3:0]));  // open: dp
  Hex_Digit_Display hex_digit_display_11 (.value(cpu_1_r2[3:0]));  // open: dp
  Hex_Digit_Display hex_digit_display_12 (.value(cpu_1_r3[3:0]));  // open: dp
  Hex_Digit_Display hex_digit_display_13 (.value(cpu_1_bus_data_2));  // open: dp
  Hex_Digit_Display hex_digit_display_14 (.value(cpu_1_ir_2));  // open: dp
  Hex_Digit_Display hex_digit_display_15 (.value(cpu_1_acc_2));  // open: dp
  Hex_Digit_Display hex_digit_display_16 (.value(cpu_1_flags));  // open: dp
  Hex_Digit_Display hex_digit_display_17 (.value(cpu_1_bus_data));  // open: dp
  Hex_Digit_Display hex_digit_display_18 (.value(cpu_1_ir));  // open: dp
  Hex_Digit_Display hex_digit_display_19 (.value(cpu_1_acc));  // open: dp

  // Notes on the sheet:
  //   contents of rom_1 (hex, n*v repeats v):
  //   20 1 24 2 28 3 2c ff 84 68 e 99 61 f e0 3b 82 68 14 e0 85 62 18 e0 84 64 1c e0 2c 20 4c e0 20 3f 24
  //   80 14 8 96 61 2a e0 20 9 24 5 28 1 a1 92 61 35 e0 20 9 24 6 28 f b1 98 61 0 e0
  //   contents of rom_2 (hex, n*v repeats v):
  //   20 19 21 9 22 f 81 96 1e e0
  //   TMP
  //   IAR
  //   R0
  //   R1
  //   R2
  //   R3
  //   BUS
  //   IR
  //   ACC
  //   FLAGS
  //   CLEZ
endmodule
